# Fritzing sketch SequencialSwitch (saved by Fritzing 0.9.3b)
circuit board: 2cm x 10.01cm
stripboards: 1

parts:
  D1 = Diode [part_number=1N5819WS package=sod-323]
  D2 = Diode [part_number=1N5819WS package=sod-323]
  C3 = Ceramic Capacitor [capacitance=10nF voltage=35V package="0603 [SMD, multilayer]"]
  C4 = Ceramic Capacitor [capacitance=10nF voltage=35V package="0603 [SMD, multilayer]"]
  C7 = Ceramic Capacitor [capacitance=10nF voltage=35V package="0603 [SMD, multilayer]"]
  R12 = Resistor [tolerance=±1% resistance=1k package="0402 [SMD]"]
  OI1 = 3.5mm Switch Jack [part_number=PJ301M-12]
  IO1 = 3.5mm Switch Jack [part_number=PJ301M-12]
  IO6 = 3.5mm Switch Jack [part_number=PJ301M-12]
  IO2 = 3.5mm Switch Jack [part_number=PJ301M-12]
  IO3 = 3.5mm Switch Jack [part_number=PJ301M-12]
  IO7 = 3.5mm Switch Jack [part_number=PJ301M-12]
  IO8 = 3.5mm Switch Jack [part_number=PJ301M-12]
  IO4 = 3.5mm Switch Jack [part_number=PJ301M-12]
  R1 = Resistor [tolerance=±1% resistance=47k package="0402 [SMD]"]
  Q2 = NPN-Transistor [part_number=2N3904 package="SOT-23 [SMD]"]
  Q1 = NPN-Transistor [part_number=2N3904 package="SOT-23 [SMD]"]
  R4 = Resistor [tolerance=±1% resistance=47k package="0402 [SMD]"]
  D3 = Diode [package=sod523]
  Q3 = NPN-Transistor [part_number=2N3904 package="SOT-23 [SMD]"]
  R5 = Resistor [tolerance=±1% resistance=10k package="0402 [SMD]"]
  R7 = Resistor [tolerance=±1% resistance=10k package="0402 [SMD]"]
  R6 = Resistor [tolerance=±1% resistance=47k package="0402 [SMD]"]
  D4 = Diode [package=sod523]
  R3 = Resistor [tolerance=±1% resistance=10k package="0402 [SMD]"]
  IC2 = SSOP16 [chip_label=DG5412 part_number=ADG5412BRUZ-REEL7 package=SSOP]
  R9 = Resistor [tolerance=±1% resistance=1k package="0402 [SMD]"]
  R10 = Resistor [tolerance=±1% resistance=1k package="0402 [SMD]"]
  R20 = Resistor [tolerance=±1% resistance=1k package="0402 [SMD]"]
  R17 = Resistor [tolerance=±1% resistance=1k package="0402 [SMD]"]
  R16 = Resistor [tolerance=±1% resistance=1k package="0402 [SMD]"]
  R13 = Resistor [tolerance=±1% resistance=1k package="0402 [SMD]"]
  R21 = Resistor [tolerance=±1% resistance=1k package="0402 [SMD]"]
  L1 = LED - 3mm [color="Red (633nm)" package="3 mm [THT]"]
  L2 = LED - 3mm [color="Red (633nm)" package="3 mm [THT]"]
  L3 = LED - 3mm [color="Red (633nm)" package="3 mm [THT]"]
  L4 = LED - 3mm [color="Red (633nm)" package="3 mm [THT]"]
  Reset = 3.5mm Switch Jack [part_number=PJ301M-12]
  Step = 3.5mm Switch Jack [part_number=PJ301M-12]
  OI2 = 3.5mm Switch Jack [part_number=PJ301M-12]
  R8 = Resistor [tolerance=±1% resistance=47k package="0402 [SMD]"]
  R2 = Resistor [tolerance=±1% resistance=10k package="0402 [SMD]"]
  C8 = Ceramic Capacitor [capacitance=10nF voltage=35V package="0603 [SMD, multilayer]"]
  C9 = Ceramic Capacitor [capacitance=10nF voltage=35V package="0603 [SMD, multilayer]"]
  D5 = Diode [package=sod523]
  IC1 = SO16 [chip_label=4017 part_number=CD4017BM96 package=SO]
  J9 = double row female pin header, 10 pins [form="♀ (female)"]
  D6 = Diode [package=sod523]
  S3 = Toggle Switch [part_number=200MSP1T1B1M2QEH package=THT]
  R11 = Resistor [tolerance=±1% resistance=1k package="0402 [SMD]"]
  IC3 = SSOP16 [chip_label=DG5412 part_number=ADG5412BRUZ-REEL7 package=SSOP]
  R19 = Resistor [tolerance=±1% resistance=1k package="0402 [SMD]"]
  C2 = Electrolytic Capacitor [capacitance=47µF part_number=CS1V100M-CRC54 package="0405 [SMD, electrolytic]"]
  C1 = Electrolytic Capacitor [capacitance=47µF voltage=35V part_number=CS1V100M-CRC54 package="0405 [SMD, electrolytic]"]
  Q4 = NPN-Transistor [part_number=2N3904 package="SOT-23 [SMD]"]
  R18 = Resistor [tolerance=±1% resistance=1k package="0402 [SMD]"]
  IO5 = 3.5mm Switch Jack [part_number=PJ301M-12]

nets:
  N1: D1.C, J9.pin5, J9.pin6
  -12V: D1.A, C3.1, IC2.4, C8.1, IC3.4, C2.-
  12V: D2.C, C4.1, C7.1, R5.Pin_0, R7.Pin_0, R3.Pin_0, IC2.12, IC2.13, R2.Pin_0, C9.1, IC1.16, IC3.12, IC3.13, C1.+
  N2: D2.A, J9.pin1, J9.pin10
  GND: C3.0, C4.0, C7.0, OI1.Pin_1, IO1.Pin_1, IO6.Pin_1, IO2.Pin_1, IO3.Pin_1, IO7.Pin_1, IO8.Pin_1, IO4.Pin_1, Q2.2, Q1.2, R4.Pin_1, Q3.2, R6.Pin_1, IC2.5, R21.Pin_0, Reset.Pin_1, Step.Pin_1, OI2.Pin_1, C8.0, C9.0, IC1.8, IC1.13, J9.pin2, J9.pin3, J9.pin4, J9.pin7, J9.pin8, J9.pin9, IC3.5, C2.+, C1.-, Q4.2, IO5.Pin_1
  N3: R12.Pin_0, IO3.Pin_3
  IO3: R12.Pin_1, IC2.11
  N4: OI1.Pin_3, R9.Pin_0
  N5: IO1.Pin_3, R10.Pin_0
  N6: IO6.Pin_3, R18.Pin_0
  N7: IO2.Pin_3, R11.Pin_0
  N8: IO7.Pin_3, R17.Pin_0
  N9: IO8.Pin_3, R16.Pin_0
  N10: IO4.Pin_3, R13.Pin_0
  N11: R1.Pin_0, Step.Pin_3
  N12: R1.Pin_1, Q2.0
  N13: Q2.1, Q1.0, R2.Pin_1
  N14: Q1.1, D3.A, R3.Pin_1
  CLK: R4.Pin_0, D3.C, IC1.14
  N15: Q3.0, R8.Pin_1
  N16: Q3.1, R7.Pin_1, Q4.0
  N17: R5.Pin_1, D4.A, Q4.1
  RES: R6.Pin_0, D4.C, D5.C, IC1.15, D6.C
  Zero: IC2.1, L1.anode, IC1.3, IC3.1
  OI: IC2.2, IC2.7, IC2.10, IC2.15, R9.Pin_1
  IO1: IC2.3, R10.Pin_1
  IO4: IC2.6, R13.Pin_1
  Tre: IC2.8, L4.anode, IC1.7, S3.L2, IC3.8
  Dos: IC2.9, L3.anode, IC1.4, S3.L1, IC3.9
  IO2: IC2.14, R11.Pin_1
  Uno: IC2.16, L2.anode, IC1.2, IC3.16
  N18: R20.Pin_0, OI2.Pin_3
  OI.: R20.Pin_1, IC3.2, IC3.7, IC3.10, IC3.15
  IO3.: R17.Pin_1, IC3.11
  IO4.: R16.Pin_1, IC3.6
  N19: R21.Pin_1, L1.cathode, L2.cathode, L3.cathode, L4.cathode
  N20: Reset.Pin_3, R8.Pin_0
  N21: D5.A, IC1.10
  N22: D6.A, S3.COM
  IO1.: IC3.3, R19.Pin_1
  IO2.: IC3.14, R18.Pin_1
  N23: R19.Pin_0, IO5.Pin_3

notes:
  -12V

custom parts:
  3.5mm Switch Jack: Thonkiconn 3.5mm switching Jack
